# Fritzing sketch tic-tac-toe (saved by Fritzing 0.9.3b)
breadboards: 1

parts:
  Pro_Trinket_3_3V = Pro Trinket 3.3V
  Pro_Trinket_LiPoly_Backpack = Adafruit Pro Trinket LiIon/LiPoly Backpack [part_number="Adafruit #2124"]
  Button_3 = Arcade Button (white)
  Button_2 = Arcade Button (white)
  Button_1 = Arcade Button (white)
  Button_4 = Arcade Button (white)
  Button_5 = Arcade Button (white)
  Button_6 = Arcade Button (white)
  Button_9 = Arcade Button (white)
  Button_8 = Arcade Button (white)
  Button_7 = Arcade Button (white)
  NeoPixel_3 = prefix0000
  NeoPixel_4 = prefix0000
  NeoPixel_2 = prefix0000
  NeoPixel_1 = prefix0000
  NeoPixel_6 = prefix0000
  NeoPixel_5 = prefix0000
  NeoPixel_9 = prefix0000
  NeoPixel_8 = prefix0000
  NeoPixel_7 = prefix0000
  Battery = LiPoly Battery (1300mAh)

nets:
  GND: Pro_Trinket_3_3V.GND, Pro_Trinket_LiPoly_Backpack.GND, Button_3.no_name_yet#2, Button_2.no_name_yet#2, Button_1.no_name_yet#2, Button_4.no_name_yet#2, Button_5.no_name_yet#2, Button_6.no_name_yet#2, Button_9.no_name_yet#2, Button_8.no_name_yet#2, Button_7.no_name_yet#2, NeoPixel_1.connector3, Battery.negative
  N1: Pro_Trinket_3_3V.VBAT, Pro_Trinket_LiPoly_Backpack.VBAT, Battery.positive
  N2: Pro_Trinket_3_3V.VBUS, Pro_Trinket_LiPoly_Backpack.VBUS
  N3: Pro_Trinket_3_3V.+3V3, NeoPixel_3.connector1, NeoPixel_4.connector1, NeoPixel_2.connector1, NeoPixel_1.connector1, NeoPixel_6.connector1, NeoPixel_5.connector1, NeoPixel_9.connector1, NeoPixel_8.connector1, NeoPixel_7.connector1
  N4: Pro_Trinket_3_3V.D6, NeoPixel_1.connector2
  N5: Pro_Trinket_3_3V.D9, Button_1.no_name_yet#1
  N6: Pro_Trinket_3_3V.D10, Button_2.no_name_yet#1
  N7: Pro_Trinket_3_3V.D11, Button_3.no_name_yet#1
  N8: Pro_Trinket_3_3V.D12, Button_4.no_name_yet#1
  N9: Pro_Trinket_3_3V.D13, Button_5.no_name_yet#1
  N10: Pro_Trinket_3_3V.A2, Button_6.no_name_yet#1
  N11: Pro_Trinket_3_3V.A3, Button_7.no_name_yet#1
  N12: Pro_Trinket_3_3V.A4, Button_8.no_name_yet#1
  N13: Pro_Trinket_3_3V.A5, Button_9.no_name_yet#1
  N14: NeoPixel_3.connector2, NeoPixel_2.connector4
  N15: NeoPixel_3.connector3, NeoPixel_4.connector3, NeoPixel_2.connector3, NeoPixel_6.connector3, NeoPixel_5.connector3, NeoPixel_9.connector3, NeoPixel_8.connector3, NeoPixel_7.connector3
  N16: NeoPixel_3.connector4, NeoPixel_4.connector2
  N17: NeoPixel_4.connector4, NeoPixel_5.connector2
  N18: NeoPixel_2.connector2, NeoPixel_1.connector4
  N19: NeoPixel_6.connector2, NeoPixel_5.connector4
  N20: NeoPixel_6.connector4, NeoPixel_7.connector2
  N21: NeoPixel_9.connector2, NeoPixel_8.connector4
  N22: NeoPixel_8.connector2, NeoPixel_7.connector4

custom parts:
  Pro Trinket 3.3V: The Pro Trinket 3.3V is like an Arduino Pro Mini with more pins and USB included. However, it uses 3V logic and 12MHz clock which means it's good when you want a lower-power and lower-voltage setup. Built with the common core Arduino chip, the ATmega328p, it has 18 GPIO, 2 extra analog inputs, 28K of flash, and 2K of RAM. It has onboard USB bootloading support with Optiboot support, so you can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
  Adafruit Pro Trinket LiIon/LiPoly Backpack: If you have a Pro Trinket you probably know it's the perfect little size for a portable project. This LiPoly backpack makes it really easy to do! Instead of wiring 2 or 3 boards together to make a charging system, this little PCB sits on top of the Pro Trinket and allows a LiPoly/LiIon battery to plug in. When the Pro Trinket USB port is powered, the battery is recharged automatically. Unplug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
  Arcade Button (white): Adafruit Arcade Button (white)
  LiPoly Battery (1300mAh): Lithium Ion Polymer Battery (1300mAh)
